// Logisim project Logisim-117-133.circ as structural Verilog: 9 circuits, main circuit main
module main (
  input  I7,
  input  I6,
  input  I5,
  input  I4,
  input  I3,
  input  I2,
  input  I1,
  input  I0,
  input  WRITE,
  input  READ,
  input  RESET,
  output O7,
  output O6,
  output O5,
  output O4,
  output O3,
  output O2,
  output O1,
  output O0,
  output EMPTY,
  output FULL,
  output OVERFLOW,
  output UNDERFLOW
);

  wire demultiplexer_1_y0, demultiplexer_1_y1, demultiplexer_1_y2, demultiplexer_1_y3, demultiplexer_1_y4,
       demultiplexer_1_y5, demultiplexer_1_y6, demultiplexer_1_y7, demultiplexer_2_1_y0,
       demultiplexer_2_1_y1, demultiplexer_2_1_y2, demultiplexer_2_1_y3, demultiplexer_2_1_y4,
       demultiplexer_2_1_y5, demultiplexer_2_1_y6, demultiplexer_2_1_y7, n2_1_mux2_1_o, n2_1_mux_1_o,
       not_1_out, not_2_out, not_3_out, register_1_check, register_2_check, register_3_check,
       register_4_check, register_5_check, register_6_check, register_7_check, register_8_check,
       upcounter_1_a0, upcounter_1_a1, upcounter_1_a2;
  wire [2:0] upcounter_2_1_a0;
  wire [7:0] register_1_output, register_2_output, register_3_output, register_4_output, register_5_output,
       register_6_output, register_7_output, register_8_output;

  not not_1 (not_1_out, 1'b1);
  _2_1_MUX u_2_1_mux_1 (.I0(WRITE), .I1(not_1_out), .S(FULL), .O(n2_1_mux_1_o));
  Upcounter upcounter_1 (
    .CLK(n2_1_mux_1_o), .PRESET(RESET), .A2(upcounter_1_a2), .A1(upcounter_1_a1), .A0(upcounter_1_a0));
  and and_1 (OVERFLOW, FULL, WRITE);
  Demultiplexer demultiplexer_1 (
    .D(n2_1_mux_1_o), .S2(upcounter_1_a2), .S1(upcounter_1_a1), .S0(upcounter_1_a0), .Y0(demultiplexer_1_y0),
    .Y1(demultiplexer_1_y1), .Y2(demultiplexer_1_y2), .Y3(demultiplexer_1_y3), .Y4(demultiplexer_1_y4),
    .Y5(demultiplexer_1_y5), .Y6(demultiplexer_1_y6), .Y7(demultiplexer_1_y7));
  nor nor_1 (EMPTY, register_1_check, register_2_check, register_3_check, register_4_check, register_5_check, register_6_check, register_7_check, register_8_check);
  Register register_1 (
    .INPUT({I7, I6, I5, I4, I3, I2, I1, I0}), .WRITE(demultiplexer_1_y0), .CHECK(register_1_check),
    .READ(demultiplexer_2_1_y0), .OUTPUT(register_1_output));
  Register register_2 (
    .INPUT({I7, I6, I5, I4, I3, I2, I1, I0}), .WRITE(demultiplexer_1_y1), .CHECK(register_2_check),
    .READ(demultiplexer_2_1_y1), .OUTPUT(register_2_output));
  Register register_3 (
    .INPUT({I7, I6, I5, I4, I3, I2, I1, I0}), .WRITE(demultiplexer_1_y2), .CHECK(register_3_check),
    .READ(demultiplexer_2_1_y2), .OUTPUT(register_3_output));
  Register register_4 (
    .INPUT({I7, I6, I5, I4, I3, I2, I1, I0}), .WRITE(demultiplexer_1_y3), .CHECK(register_4_check),
    .READ(demultiplexer_2_1_y3), .OUTPUT(register_4_output));
  Register register_5 (
    .INPUT({I7, I6, I5, I4, I3, I2, I1, I0}), .WRITE(demultiplexer_1_y4), .CHECK(register_5_check),
    .READ(demultiplexer_2_1_y4), .OUTPUT(register_5_output));
  Register register_6 (
    .INPUT({I7, I6, I5, I4, I3, I2, I1, I0}), .WRITE(demultiplexer_1_y5), .CHECK(register_6_check),
    .READ(demultiplexer_2_1_y5), .OUTPUT(register_6_output));
  Register register_7 (
    .INPUT({I7, I6, I5, I4, I3, I2, I1, I0}), .WRITE(demultiplexer_1_y6), .CHECK(register_7_check),
    .READ(demultiplexer_2_1_y6), .OUTPUT(register_7_output));
  Register register_8 (
    .INPUT({I7, I6, I5, I4, I3, I2, I1, I0}), .WRITE(demultiplexer_1_y7), .CHECK(register_8_check),
    .READ(demultiplexer_2_1_y7), .OUTPUT(register_8_output));
  and and_2 (FULL, register_1_check, register_2_check, register_3_check, register_4_check, register_5_check, register_6_check, register_7_check, register_8_check);
  Demultiplexer_2 demultiplexer_2_1 (
    .D(n2_1_mux2_1_o), .S2(upcounter_2_1_a0[2]), .S1(upcounter_2_1_a0[1]), .S0(upcounter_2_1_a0[0]),
    .Y0(demultiplexer_2_1_y0), .Y1(demultiplexer_2_1_y1), .Y2(demultiplexer_2_1_y2),
    .Y3(demultiplexer_2_1_y3), .Y4(demultiplexer_2_1_y4), .Y5(demultiplexer_2_1_y5),
    .Y6(demultiplexer_2_1_y6), .Y7(demultiplexer_2_1_y7));
  Upcounter_2 upcounter_2_1 (
    .CLK(n2_1_mux2_1_o), .PRESET(RESET), .A2(upcounter_2_1_a0[2]), .A1(upcounter_2_1_a0[1]),
    .A0(upcounter_2_1_a0[0]));
  and and_3 (UNDERFLOW, EMPTY, not_3_out);
  _2_1_MUX2 u_2_1_mux2_1 (.O(n2_1_mux2_1_o), .S(EMPTY), .I0(READ), .I1(not_2_out));
  not not_2 (not_2_out, 1'b1);
  Multiplexer_part #(.select(3), .width(8)) multiplexer_1 (
    .in0(register_1_output), .in1(register_2_output), .in2(register_3_output), .in3(register_4_output),
    .in4(register_5_output), .in5(register_6_output), .in6(register_7_output), .in7(register_8_output),
    .out({O7, O6, O5, O4, O3, O2, O1, O0}), .sel(upcounter_2_1_a0));  // open: en
  not not_3 (not_3_out, READ);

  // Notes on the sheet:
  //   INPUT(8-bits)
  //   OVERFLOW condition
  //   FIFO MEMORY
  //   16CO117-16CO133
  //   UNDERFLOW condition
  //   OUTPUT(8-bits)
endmodule

// REG
module Register (
  input  [7:0] INPUT,
  input  READ,
  input  WRITE,
  output [7:0] OUTPUT,
  output CHECK
);

  or or_1 (CHECK, OUTPUT[7], OUTPUT[6], OUTPUT[5], OUTPUT[4], OUTPUT[3], OUTPUT[2], OUTPUT[1], OUTPUT[0]);
  D_Flip_Flop d_ff_1 (.clk(WRITE), .D(INPUT[7]), .Q(OUTPUT[7]), .en(WRITE), .reset(READ));  // open: Qn, preset
  D_Flip_Flop d_ff_2 (.clk(WRITE), .D(INPUT[6]), .Q(OUTPUT[6]), .en(WRITE), .reset(READ));  // open: Qn, preset
  D_Flip_Flop d_ff_3 (.clk(WRITE), .D(INPUT[5]), .Q(OUTPUT[5]), .en(WRITE), .reset(READ));  // open: Qn, preset
  D_Flip_Flop d_ff_4 (.clk(WRITE), .D(INPUT[4]), .Q(OUTPUT[4]), .en(WRITE), .reset(READ));  // open: Qn, preset
  D_Flip_Flop d_ff_5 (.clk(WRITE), .D(INPUT[3]), .Q(OUTPUT[3]), .en(WRITE), .reset(READ));  // open: Qn, preset
  D_Flip_Flop d_ff_6 (.clk(WRITE), .D(INPUT[2]), .Q(OUTPUT[2]), .en(WRITE), .reset(READ));  // open: Qn, preset
  D_Flip_Flop d_ff_7 (.clk(WRITE), .D(INPUT[1]), .Q(OUTPUT[1]), .en(WRITE), .reset(READ));  // open: Qn, preset
  D_Flip_Flop d_ff_8 (.clk(WRITE), .D(INPUT[0]), .Q(OUTPUT[0]), .en(WRITE), .reset(READ));  // open: Qn, preset

  // Notes on the sheet:
  //   This is a register which stores 8 bits in 8 D-flipflops
  //    REGISTER
endmodule

module Multiplexer (
  input  I0,
  input  I1,
  input  I2,
  input  I3,
  input  I4,
  input  I5,
  input  I6,
  input  I7,
  input  S2,
  input  S1,
  input  S0,
  output Y
);

  wire and_1_out, and_2_out, and_3_out, and_4_out, and_5_out, and_6_out, and_7_out, and_8_out, not_1_out,
       not_2_out, not_3_out;

  not not_1 (not_1_out, S0);
  not not_2 (not_2_out, S1);
  not not_3 (not_3_out, S2);
  and and_1 (and_1_out, not_1_out, not_2_out, not_3_out, I0);
  and and_2 (and_2_out, S0, not_2_out, not_3_out, I1);
  and and_3 (and_3_out, not_1_out, S1, not_3_out, I2);
  and and_4 (and_4_out, S0, S1, not_3_out, I3);
  and and_5 (and_5_out, not_1_out, not_2_out, S2, I4);
  and and_6 (and_6_out, S0, not_2_out, S2, I5);
  and and_7 (and_7_out, not_1_out, S1, S2, I6);
  and and_8 (and_8_out, S0, S1, S2, I7);
  or or_1 (Y, and_1_out, and_2_out, and_3_out, and_4_out, and_5_out, and_6_out, and_7_out, and_8_out);

  // Notes on the sheet:
  //   This is a 8-1 multiplexer which is used to select outputs
  //   MULTIPLEXER
endmodule

// D1
module Demultiplexer (
  input  D,
  input  S2,
  input  S1,
  input  S0,
  output Y0,
  output Y1,
  output Y2,
  output Y3,
  output Y4,
  output Y5,
  output Y6,
  output Y7
);

  wire not_1_out, not_2_out, not_3_out, not_4_out;

  not not_1 (not_1_out, D);
  not not_2 (not_2_out, S2);
  not not_3 (not_3_out, S1);
  not not_4 (not_4_out, S0);
  and and_1 (Y0, not_1_out, not_2_out, not_3_out, not_4_out);
  and and_2 (Y1, not_1_out, not_2_out, not_3_out, S0);
  and and_3 (Y2, not_1_out, not_2_out, S1, not_4_out);
  and and_4 (Y3, not_1_out, not_2_out, S1, S0);
  and and_5 (Y4, not_1_out, S2, not_3_out, not_4_out);
  and and_6 (Y5, not_1_out, S2, not_3_out, S0);
  and and_7 (Y6, not_1_out, S2, S1, not_4_out);
  and and_8 (Y7, not_1_out, S2, S1, S0);

  // Notes on the sheet:
  //   DEMULTIPLEXER
  //   This is a 1-8 demultiplexer used to select the write pointer
endmodule

// C1
module Upcounter (
  input  CLK,
  input  PRESET,
  output A2,
  output A1,
  output A0
);

  wire and_1_out;

  T_Flip_Flop t_ff_1 (.clk(CLK), .T(and_1_out), .Q(A2), .preset(PRESET));  // open: Qn, reset, en
  and and_1 (and_1_out, A0, A1);
  T_Flip_Flop t_ff_2 (.clk(CLK), .T(A0), .Q(A1), .preset(PRESET));  // open: Qn, reset, en
  T_Flip_Flop t_ff_3 (.clk(CLK), .T(1'b1), .Q(A0), .preset(PRESET));  // open: Qn, reset, en

  // Notes on the sheet:
  //   UP COUNTER
  //   This is an upcounter used to keep count of write pointer
endmodule

// D2
module Demultiplexer_2 (
  input  D,
  input  S2,
  input  S1,
  input  S0,
  output Y0,
  output Y1,
  output Y2,
  output Y3,
  output Y4,
  output Y5,
  output Y6,
  output Y7
);

  wire not_1_out, not_2_out, not_3_out, not_4_out;

  not not_1 (not_1_out, D);
  not not_2 (not_2_out, S2);
  not not_3 (not_3_out, S1);
  not not_4 (not_4_out, S0);
  and and_1 (Y0, not_1_out, not_2_out, not_3_out, not_4_out);
  and and_2 (Y1, not_1_out, not_2_out, not_3_out, S0);
  and and_3 (Y2, not_1_out, not_2_out, S1, not_4_out);
  and and_4 (Y3, not_1_out, not_2_out, S1, S0);
  and and_5 (Y4, not_1_out, S2, not_3_out, not_4_out);
  and and_6 (Y5, not_1_out, S2, not_3_out, S0);
  and and_7 (Y6, not_1_out, S2, S1, not_4_out);
  and and_8 (Y7, not_1_out, S2, S1, S0);

  // Notes on the sheet:
  //   This is a 1-8 demultiplexer used to select the read pointer
  //   DEMULTIPLEXER
endmodule

// C2
module Upcounter_2 (
  input  CLK,
  input  PRESET,
  output A2,
  output A1,
  output A0
);

  wire and_1_out;

  T_Flip_Flop t_ff_1 (.clk(CLK), .T(and_1_out), .Q(A2), .preset(PRESET));  // open: Qn, reset, en
  and and_1 (and_1_out, A0, A1);
  T_Flip_Flop t_ff_2 (.clk(CLK), .T(A0), .Q(A1), .preset(PRESET));  // open: Qn, reset, en
  T_Flip_Flop t_ff_3 (.clk(CLK), .T(1'b1), .Q(A0), .preset(PRESET));  // open: Qn, reset, en

  // Notes on the sheet:
  //   UP COUNTER
  //   This is an upcounter used to keep count of read pointer
endmodule

// M1
module _2_1_MUX (
  input  I0,
  input  I1,
  input  S,
  output O
);

  wire and_1_out, and_2_out, not_1_out;

  not not_1 (not_1_out, S);
  and and_1 (and_1_out, I0, not_1_out);
  and and_2 (and_2_out, I1, S);
  or or_1 (O, and_1_out, and_2_out);

  // Notes on the sheet:
  //   2-1_MULTIPLEXER
  //   This is a 2-1 multiplexer used for overflow detection
endmodule

// M2
module _2_1_MUX2 (
  input  I0,
  input  I1,
  input  S,
  output O
);

  wire and_1_out, and_2_out, not_1_out;

  or or_1 (O, and_2_out, and_1_out);
  and and_1 (and_1_out, S, I1);
  and and_2 (and_2_out, I0, not_1_out);
  not not_1 (not_1_out, S);

  // Notes on the sheet:
  //   2-1_MULTIPLEXER
  //   This is a 2-1 multiplexer used for underflow detection
endmodule
